# Fritzing sketch rpi-ballotbox (saved by Fritzing 0.9.3b)
breadboards: 1

parts:
  V1 = DC Power [voltage=12V]
  Switching_regulator = Voltage Regulator - 5V [part_number=PT78ST105H package="TO220 [THT]"]
  IC1 = L293D [package=THT]
  Raspberry_Pi1 = Raspberry Pi 2
  Sheet_feeder = DC Motor [part_number="HP J110a"]
  D1 = Rectifier Diode [part_number=1N4001 package="300 mil [THT]"]
  D2 = Rectifier Diode [part_number=1N4001 package="300 mil [THT]"]
  D3 = Rectifier Diode [part_number=1N4001 package="300 mil [THT]"]
  D4 = Rectifier Diode [part_number=1N4001 package="300 mil [THT]"]
  2A = Fuse with Handler
  Power_button = Pushbutton [package=THT]
  Feed_motor_sensor = PHOTOTRANSISTOR REFLECTIVE OBJECT SENSOR [part_number="HP J110a" package=qrb1114-side]
  R1 = Resistor [tolerance=±5% resistance=220 package=THT]
  R2 = Resistor [tolerance=±5% resistance=7.5k package=THT]
  Diverter_servo = Basic Servo [part_number="Futaba S3003"]

nets:
  N1: V1.V+, IC1.+Vmotor, D1.cathode, D2.cathode, 2A.Connector1
  GND: V1.V-, Switching_regulator.GND, IC1.0V, Raspberry_Pi1.GND, D3.anode, D4.anode, Power_button.leg1, Feed_motor_sensor.E, Feed_motor_sensor.K, Diverter_servo.gnd
  N2: Switching_regulator.input_voltage, 2A.Connector2
  5V: Switching_regulator.output_voltage, IC1.+V, Raspberry_Pi1.5V, R1.Pin_0, R2.Pin_0, Diverter_servo.vcc
  N3: IC1.Enable_1, Raspberry_Pi1.GPIO17
  N4: IC1.In_1, Raspberry_Pi1.GPIO27
  N5: IC1.Out_1_(_Controlled_by_Enable_1_), Sheet_feeder.pin_1, D1.anode, D3.cathode
  N6: IC1.Out_2_(_Controlled_by_Enable_1_), Sheet_feeder.pin_2, D2.anode, D4.cathode
  N7: IC1.In_2, Raspberry_Pi1.GPIO22
  N8: Raspberry_Pi1.GPIO3, Power_button.leg0
  N9: Raspberry_Pi1.GPIO23, Feed_motor_sensor.C, R2.Pin_1
  N10: Raspberry_Pi1.GPIO18, Diverter_servo.pulse
  N11: Feed_motor_sensor.A, R1.Pin_1
